# Fritzing sketch ATBoard (saved by Fritzing 0.9.2b)
breadboards: 1
perfboards: 1

parts:
  Bauteil1 = Arduino Nano (Rev3.0)
  U1 = RS232 Transceiver [package=dil16]
  C1 = Electrolytic Capacitor [capacitance=1µF package="100 mil [THT, electrolytic]"]  # not connected
  C2 = Electrolytic Capacitor [capacitance=1µF package="100 mil [THT, electrolytic]"]  # not connected
  JP1 = Header 4 [package=screwterminal-3.5mm-4_lock]  # not connected
  J1 = COMPUTER-PERIPHERAL-POWER [package=computer-peripheral-power]
  S1 = Pushbutton [package="[THT]"]
  S2 = Pushbutton [package="[SMD]"]
  S3 = Pushbutton [package="[SMD]"]
  S4 = Pushbutton [package="[SMD]"]
  S5 = Pushbutton [package="[SMD]"]
  S6 = Pushbutton [package="[SMD]"]

nets:
  N1: Bauteil1.D1/TX, U1.T1IN
  N2: Bauteil1.D0/RX, U1.R1OUT
  N3: Bauteil1.D10, S2.Pin_3, S2.Pin_4
  N4: Bauteil1.D11/MOSI, S1.Pin_3, S1.Pin_4
  5V: Bauteil1.5V, U1.VCC
  N5: U1.R1IN, J1.RxD
  N6: U1.T1OUT, J1.TxD
  N7: S1.Pin_1, S1.Pin_2
  N8: S2.Pin_1, S2.Pin_2
  N9: S3.Pin_1, S3.Pin_2
  N10: S3.Pin_3, S3.Pin_4
  N11: S4.Pin_1, S4.Pin_2
  N12: S4.Pin_3, S4.Pin_4
  N13: S5.Pin_1, S5.Pin_2
  N14: S5.Pin_3, S5.Pin_4
  N15: S6.Pin_1, S6.Pin_2
  N16: S6.Pin_3, S6.Pin_4
