# Fritzing sketch Schalterplatine (saved by Fritzing 0.9.2b)
circuit board: 2.4709cm x 2.95058cm
perfboards: 1

parts:
  J1 = shrouded pin header, 10 pins [form="♂ (shrouded male)"]
  J2 = male pin header, 8 pins [form="♂ (male)"]
  J3 = male pin header, 8 pins [form="♂ (male)"]

nets:
  N1: J1.pin1, J3.pin6
  N2: J1.pin2, J2.pin8
  N3: J1.pin3, J3.pin8
  N4: J1.pin4, J3.pin7
  N5: J1.pin5, J2.pin1, J2.pin3, J2.pin5, J2.pin7, J3.pin1, J3.pin3, J3.pin5
  N6: J1.pin6, J3.pin4
  N7: J1.pin7, J3.pin2
  N8: J1.pin8, J2.pin2
  N9: J1.pin9, J2.pin4
  N10: J1.pin10, J2.pin6

notes:
  SDL
  SCL
  GND
  PWD
